# Fritzing sketch schema_L1Dcube (saved by Fritzing 0.9.6b)
perfboards: 1

parts:
  LED2 = LED - 5mm [color="Red (633nm)" current=20mA package="5 mm [THT]"]
  LED1 = LED - 5mm [color="Green (555nm)" current=20mA package="5 mm [THT]"]
  R2 = Resistor [tolerance=±5% power=0.25W resistance=51 package=THT]
  1_3"_128x64_OLED = Module display OLED I2C 128x64 SSD1306 [package=THT]  # not connected
  SDA_SCK_GND_VDD = male pin header, 4 pins [form="♂ (male)"]
  D1_mini_v4_0_0 = WeMos D1 Mini V4.0.0
  R1 = Resistor [tolerance=±5% power=0.25W resistance=15 package=THT]

nets:
  N1: LED2.cathode, R2.Pin_0
  N2: LED2.anode, D1_mini_v4_0_0.12/MISO
  N3: LED1.cathode, R1.Pin_0
  N4: LED1.anode, D1_mini_v4_0_0.14/SCK
  N5: SDA_SCK_GND_VDD.pin1, D1_mini_v4_0_0.4/SDA
  N6: SDA_SCK_GND_VDD.pin2, D1_mini_v4_0_0.5/SCL
  N7: SDA_SCK_GND_VDD.pin4, D1_mini_v4_0_0.3.3V

notes:
  černá/hnědá
  VDD červený s konektorem 7cm
  SDA žlutý s konektorem 7cm
  SCK(SCL) bílý s konektorem 7cm
  GND OLED černý/hnědý s konektorem 7cm
  zelená LED zelený 4cm
  červená LED oranžový 6cm
  GND černý 5cm
  3V3 VCC
  14 zelená LED
  12 červená LED
  5 SCL/SCK
  4 SDA
  GND
  5
  4
  3V3
  14
  12
  OLED

custom parts:
  Module display OLED I2C 128x64 SSD1306: Ecran OLED I2C SSD163 de 128x64 avec connexion I2C
  WeMos D1 Mini V4.0.0: The D1 mini is a mini wifi board based on ESP-8266EX.
