# Fritzing sketch schema_L1Dcube_LED_PCB (saved by Fritzing 0.9.6b)
perfboards: 1

parts:
  LED2 = LED - 5mm [color="Red (633nm)" current=20mA package="5 mm [THT]"]
  LED1 = LED - 5mm [color="Green (555nm)" current=20mA package="5 mm [THT]"]
  R2 = Resistor [tolerance=±5% power=0.25W resistance=51 package=THT]
  R1 = Resistor [tolerance=±5% power=0.25W resistance=15 package=THT]

nets:
  N1: LED2.cathode, R2.Pin_0
  N2: LED1.cathode, R1.Pin_0
  N3: R2.Pin_1, R1.Pin_1

notes:
  OLED
  GND
